// Logisim project 21-bit-ALU.circ as structural Verilog: 13 circuits, main circuit ALU
module ALU (
  input  c2,
  input  c1,
  input  c0,
  input  [20:0] A,
  input  [20:0] B,
  output [20:0] Result,
  output Zero,
  output Negative,
  output Overflow,
  output Carry
);

  _21_bit_ALU u_21_bit_alu_1 (
    .A(A), .B(B), .Result(Result), .Zero(Zero), .Negative(Negative), .Overflow(Overflow), .Carry(Carry),
    .Control2(c2), .Control1(c1), .control0(c0));
endmodule

// 21-bit AND/OR
module _21_bit_and_or (
  input  Add_Or,
  input  [20:0] A,
  input  [20:0] B,
  output [20:0] Result
);

  wire [20:0] and_1_out, or_1_out;

  assign and_1_out = A & B;  // AND_Gate and_1, 21 bits wide
  assign or_1_out = A | B;  // OR_Gate or_1, 21 bits wide
  Multiplexer #(.width(21), .enable("false")) multiplexer_1 (
    .in0(or_1_out), .in1(and_1_out), .out(Result), .sel(Add_Or));
endmodule

// 21-bit OR
module _21_bit_OR (
  input  [20:0] A,
  input  [20:0] B,
  output [20:0] Result
);

  or or_1 (Result[0], A[0], B[0]);
  or or_2 (Result[1], A[1], B[1]);
  or or_3 (Result[2], A[2], B[2]);
  or or_4 (Result[3], A[3], B[3]);
  or or_5 (Result[4], A[4], B[4]);
  or or_6 (Result[5], A[5], B[5]);
  or or_7 (Result[6], A[6], B[6]);
  or or_8 (Result[7], A[7], B[7]);
  or or_9 (Result[8], A[8], B[8]);
  or or_10 (Result[9], A[9], B[9]);
  or or_11 (Result[10], A[10], B[10]);
  or or_12 (Result[11], A[11], B[11]);
  or or_13 (Result[12], A[12], B[12]);
  or or_14 (Result[13], A[13], B[13]);
  or or_15 (Result[14], A[14], B[14]);
  or or_16 (Result[15], A[15], B[15]);
  or or_17 (Result[16], A[16], B[16]);
  or or_18 (Result[17], A[17], B[17]);
  or or_19 (Result[18], B[18], A[18]);
  or or_20 (Result[19], A[19], B[19]);
  or or_21 (Result[20], A[20], B[20]);
endmodule

module Full_adder (
  input  Carry_in,
  input  A,
  input  B,
  output Result,
  output Carry_out
);

  wire and_1_out, and_2_out, xor_1_out;

  and and_1 (and_1_out, B, A);
  xor xor_1 (xor_1_out, A, B);
  or or_1 (Carry_out, and_1_out, and_2_out);
  and and_2 (and_2_out, xor_1_out, Carry_in);
  xor xor_2 (Result, Carry_in, xor_1_out);
endmodule

// FA
module _21_bit_full_adder_concise (
  input  [20:0] A,
  input  Carry_in,
  input  [20:0] B,
  output [20:0] Result,
  output Carry
);

  wire full_adder_1_carry_out, full_adder_2_carry_out, full_adder_3_carry_out, full_adder_4_carry_out,
       full_adder_5_carry_out, full_adder_6_carry_out, full_adder_7_carry_out, full_adder_8_carry_out,
       full_adder_9_carry_out, full_adder_10_carry_out, full_adder_11_carry_out, full_adder_12_carry_out,
       full_adder_13_carry_out, full_adder_14_carry_out, full_adder_15_carry_out, full_adder_16_carry_out,
       full_adder_17_carry_out, full_adder_18_carry_out, full_adder_19_carry_out, full_adder_20_carry_out;

  Full_adder full_adder_1 (
    .Carry_in(Carry_in), .A(A[0]), .B(B[0]), .Result(Result[0]), .Carry_out(full_adder_1_carry_out));
  Full_adder full_adder_2 (
    .Carry_in(full_adder_1_carry_out), .A(A[1]), .B(B[1]), .Result(Result[1]),
    .Carry_out(full_adder_2_carry_out));
  Full_adder full_adder_3 (
    .Carry_in(full_adder_2_carry_out), .A(A[2]), .B(B[2]), .Result(Result[2]),
    .Carry_out(full_adder_3_carry_out));
  Full_adder full_adder_4 (
    .Carry_in(full_adder_3_carry_out), .A(A[3]), .B(B[3]), .Result(Result[3]),
    .Carry_out(full_adder_4_carry_out));
  Full_adder full_adder_5 (
    .Carry_in(full_adder_4_carry_out), .A(A[4]), .B(B[4]), .Result(Result[4]),
    .Carry_out(full_adder_5_carry_out));
  Full_adder full_adder_6 (
    .Carry_in(full_adder_5_carry_out), .A(A[5]), .B(B[5]), .Result(Result[5]),
    .Carry_out(full_adder_6_carry_out));
  Full_adder full_adder_7 (
    .Carry_in(full_adder_6_carry_out), .A(A[6]), .B(B[6]), .Result(Result[6]),
    .Carry_out(full_adder_7_carry_out));
  Full_adder full_adder_8 (
    .Carry_in(full_adder_7_carry_out), .A(A[7]), .B(B[7]), .Result(Result[7]),
    .Carry_out(full_adder_8_carry_out));
  Full_adder full_adder_9 (
    .Carry_in(full_adder_8_carry_out), .A(A[8]), .B(B[8]), .Result(Result[8]),
    .Carry_out(full_adder_9_carry_out));
  Full_adder full_adder_10 (
    .Carry_in(full_adder_9_carry_out), .A(A[9]), .B(B[9]), .Result(Result[9]),
    .Carry_out(full_adder_10_carry_out));
  Full_adder full_adder_11 (
    .Carry_in(full_adder_10_carry_out), .A(A[10]), .B(B[10]), .Result(Result[10]),
    .Carry_out(full_adder_11_carry_out));
  Full_adder full_adder_12 (
    .Carry_in(full_adder_11_carry_out), .A(A[11]), .B(B[11]), .Result(Result[11]),
    .Carry_out(full_adder_12_carry_out));
  Full_adder full_adder_13 (
    .Carry_in(full_adder_12_carry_out), .A(A[12]), .B(B[12]), .Result(Result[12]),
    .Carry_out(full_adder_13_carry_out));
  Full_adder full_adder_14 (
    .Carry_in(full_adder_13_carry_out), .A(A[13]), .B(B[13]), .Result(Result[13]),
    .Carry_out(full_adder_14_carry_out));
  Full_adder full_adder_15 (
    .Carry_in(full_adder_14_carry_out), .A(A[14]), .B(B[14]), .Result(Result[14]),
    .Carry_out(full_adder_15_carry_out));
  Full_adder full_adder_16 (
    .Carry_in(full_adder_15_carry_out), .A(A[15]), .B(B[15]), .Result(Result[15]),
    .Carry_out(full_adder_16_carry_out));
  Full_adder full_adder_17 (
    .Carry_in(full_adder_16_carry_out), .A(A[16]), .B(B[16]), .Result(Result[16]),
    .Carry_out(full_adder_17_carry_out));
  Full_adder full_adder_18 (
    .Carry_in(full_adder_17_carry_out), .A(A[17]), .B(B[17]), .Result(Result[17]),
    .Carry_out(full_adder_18_carry_out));
  Full_adder full_adder_19 (
    .Carry_in(full_adder_18_carry_out), .A(A[18]), .B(B[18]), .Result(Result[18]),
    .Carry_out(full_adder_19_carry_out));
  Full_adder full_adder_20 (
    .Carry_in(full_adder_19_carry_out), .A(A[19]), .B(B[19]), .Result(Result[19]),
    .Carry_out(full_adder_20_carry_out));
  Full_adder full_adder_21 (
    .Carry_in(full_adder_20_carry_out), .A(A[20]), .B(B[20]), .Result(Result[20]), .Carry_out(Carry));
endmodule

module _21_bit_xor (
  input  Control,
  input  [20:0] B,
  output [20:0] Result
);

  xor xor_1 (Result[0], Control, B[0]);
  xor xor_2 (Result[1], Control, B[1]);
  xor xor_3 (Result[2], Control, B[2]);
  xor xor_4 (Result[3], Control, B[3]);
  xor xor_5 (Result[4], Control, B[4]);
  xor xor_6 (Result[5], Control, B[5]);
  xor xor_7 (Result[6], Control, B[6]);
  xor xor_8 (Result[7], Control, B[7]);
  xor xor_9 (Result[8], Control, B[8]);
  xor xor_10 (Result[9], Control, B[9]);
  xor xor_11 (Result[10], Control, B[10]);
  xor xor_12 (Result[11], Control, B[11]);
  xor xor_13 (Result[12], Control, B[12]);
  xor xor_14 (Result[13], Control, B[13]);
  xor xor_15 (Result[14], Control, B[14]);
  xor xor_16 (Result[15], Control, B[15]);
  xor xor_17 (Result[16], Control, B[16]);
  xor xor_18 (Result[17], Control, B[17]);
  xor xor_19 (Result[18], B[18], Control);
  xor xor_20 (Result[19], Control, B[19]);
  xor xor_21 (Result[20], Control, B[20]);
endmodule

// 21-bit \nSub/add
module Add_sub (
  input  Sub,
  input  [20:0] A,
  input  [20:0] B,
  output [20:0] Result,
  output Carry,
  output Overflow
);

  wire and_1_out, and_2_out, n20th_bit_out_1__20th_bit, n20th_bit_out_2__20th_bit, n20th_bit_out_3__20th_bit,
       not_1_out, not_2_out, not_3_out;
  wire [20:0] n21_bit_xor_1_result;

  _20th_bit_out u_20th_bit_out_1 (.Input(A), ._20th_bit(n20th_bit_out_1__20th_bit));
  not not_1 (not_1_out, n20th_bit_out_1__20th_bit);
  _20th_bit_out u_20th_bit_out_2 (.Input(B), ._20th_bit(n20th_bit_out_2__20th_bit));
  not not_2 (not_2_out, n20th_bit_out_2__20th_bit);
  _21_bit_full_adder_concise u_21_bit_full_adder_concise_1 (
    .A(A), .B(n21_bit_xor_1_result), .Result(Result), .Carry_in(Sub), .Carry(Carry));
  _21_bit_xor u_21_bit_xor_1 (.Control(Sub), .B(B), .Result(n21_bit_xor_1_result));
  _20th_bit_out u_20th_bit_out_3 (.Input(Result), ._20th_bit(n20th_bit_out_3__20th_bit));
  not not_3 (not_3_out, n20th_bit_out_3__20th_bit);
  and and_1 (and_1_out, not_3_out, n20th_bit_out_2__20th_bit, n20th_bit_out_1__20th_bit);
  and and_2 (and_2_out, n20th_bit_out_3__20th_bit, not_2_out, not_1_out);
  or or_1 (Overflow, and_1_out, and_2_out);

  // Notes on the sheet:
  //   A31
  //   B31
  //   Result 31
endmodule

// 20th
module _20th_bit_out (
  input  [20:0] Input,
  output _20th_bit
);


  assign _20th_bit = Input[20];
endmodule

// Reduce-OR
module _32_bit_reduce_or (
  input  [20:0] Input,
  output Output
);

  or or_1 (Output, Input[0], Input[1], Input[2], Input[3], Input[4], Input[5], Input[6], Input[7], Input[8], Input[9], Input[10], Input[11], Input[12], Input[13], Input[14], Input[15], Input[16], Input[17], Input[18], Input[19], Input[20]);
endmodule

module _21_bit_ALU (
  input  control0,
  input  Control2,
  input  Control1,
  input  [20:0] A,
  input  [20:0] B,
  output [20:0] Result,
  output Zero,
  output Negative,
  output Overflow,
  output Carry
);

  wire car_s_a, inc_dec_a_1_carry, inc_dec_a_1_overflow, n32_bit_reduce_or_1_output, not_1_out, o_s_d;
  wire [20:0] add_sub_1_result, inc_dec_a_1_result, left_shift_1_output, n21_bit_and_or_1_result;

  _21_bit_and_or u_21_bit_and_or_1 (.A(A), .B(B), .Result(n21_bit_and_or_1_result), .Add_Or(control0));
  Add_sub add_sub_1 (.Sub(control0), .A(A), .B(B), .Result(add_sub_1_result), .Carry(car_s_a), .Overflow(o_s_d));
  not not_1 (not_1_out, control0);
  Inc_Dec_A inc_dec_a_1 (
    .Dec(not_1_out), .A(A), .Result(inc_dec_a_1_result), .Carry(inc_dec_a_1_carry),
    .Overflow(inc_dec_a_1_overflow));
  left_shift left_shift_1 (.A(A), .Output(left_shift_1_output), .B(B), .xor_left_shift(control0));
  Multiplexer #(.select(2), .width(21), .enable("false")) multiplexer_1 (
    .in0(n21_bit_and_or_1_result), .in1(add_sub_1_result), .in2(inc_dec_a_1_result),
    .in3(left_shift_1_output), .out(Result), .sel({Control2, Control1}));
  _20th_bit_out u_20th_bit_out_1 (.Input(Result), ._20th_bit(Negative));
  Multiplexer #(.enable("false")) multiplexer_2 (
    .in0(inc_dec_a_1_overflow), .in1(o_s_d), .out(Overflow), .sel(Control1));
  _32_bit_reduce_or u_32_bit_reduce_or_1 (.Input(Result), .Output(n32_bit_reduce_or_1_output));
  not not_2 (Zero, n32_bit_reduce_or_1_output);
  Multiplexer #(.enable("false")) multiplexer_3 (.in0(inc_dec_a_1_carry), .in1(car_s_a), .out(Carry), .sel(Control1));

  // Other names for the same wires on the sheet: c1 = Control1
endmodule

// Inc/Dec
module Inc_Dec_A (
  input  Dec,
  input  [20:0] A,
  output [20:0] Result,
  output Carry,
  output Overflow
);

  wire and_1_out, and_2_out, n20th_bit_out_1__20th_bit, n20th_bit_out_2__20th_bit, n20th_bit_out_3__20th_bit,
       not_1_out, not_2_out, not_3_out;
  wire [20:0] n21_bit_xor_1_result;

  _20th_bit_out u_20th_bit_out_1 (.Input(A), ._20th_bit(n20th_bit_out_1__20th_bit));
  not not_1 (not_1_out, n20th_bit_out_1__20th_bit);
  _20th_bit_out u_20th_bit_out_2 (.Input(21'h1), ._20th_bit(n20th_bit_out_2__20th_bit));
  not not_2 (not_2_out, n20th_bit_out_2__20th_bit);
  _21_bit_full_adder_concise u_21_bit_full_adder_concise_1 (
    .A(A), .B(n21_bit_xor_1_result), .Result(Result), .Carry_in(Dec), .Carry(Carry));
  _21_bit_xor u_21_bit_xor_1 (.Control(Dec), .B(21'h1), .Result(n21_bit_xor_1_result));
  _20th_bit_out u_20th_bit_out_3 (.Input(Result), ._20th_bit(n20th_bit_out_3__20th_bit));
  not not_3 (not_3_out, n20th_bit_out_3__20th_bit);
  and and_1 (and_1_out, not_3_out, n20th_bit_out_2__20th_bit, n20th_bit_out_1__20th_bit);
  and and_2 (and_2_out, n20th_bit_out_3__20th_bit, not_2_out, not_1_out);
  or or_1 (Overflow, and_1_out, and_2_out);

  // Notes on the sheet:
  //   A31
  //   B31
  //   Result 31
endmodule

// 21_bit_xor
module _21_bit_xor_2 (
  input  [20:0] A,
  input  [20:0] B,
  output [20:0] Output
);

  assign Output = A ^ B;  // XOR_Gate xor_1, 21 bits wide
endmodule

// 21_xor/left_shift
module left_shift (
  input  [20:0] B,
  input  xor_left_shift,
  input  [20:0] A,
  output [20:0] Output
);

  wire [20:0] xor_1_out;

  assign xor_1_out = B ^ A;  // XOR_Gate xor_1, 21 bits wide
  Multiplexer #(.width(21), .enable("false")) multiplexer_1 (
    .in0({A[19:0], 1'b0}), .in1(xor_1_out), .out(Output), .sel(xor_left_shift));
endmodule
