// Logisim project Booths_multiplication.circ as structural Verilog: 8 circuits, main circuit Booth's multiplier
module Booth_s_multiplier (
  input  [20:0] M_input,
  input  [20:0] Q_input,
  input  Reset,
  input  clk,
  output [20:0] LSB,
  output Multiplying,
  output [20:0] MSB
);

  wire A_out, controller_1_c0, controller_1_c1, controller_1_cl__a__q_1, controller_1_dec_cnt,
       controller_1_load__m__q__cnt, controller_1_load_a, controller_1_shr, or_2_out, Q__1_q0, Q_out;
  wire [4:0] counter_1_q;
  wire [20:0] _21_bit_alu_p5, M_q20;

  or or_1 (Multiplying, counter_1_q[0], counter_1_q[1], counter_1_q[2], counter_1_q[3], counter_1_q[4]);
  Controller controller_1 (
    .Clk(clk), .Q0(LSB[0]), .Q_1(Q__1_q0), .Count(counter_1_q), .C0(controller_1_c0), .C1(controller_1_c1),
    .Shr(controller_1_shr), .Dec_Cnt(controller_1_dec_cnt), .Cl__A__Q_1(controller_1_cl__a__q_1),
    .Load_A(controller_1_load_a), .LOad__M__Q__Cnt(controller_1_load__m__q__cnt), .Reset(Reset));
  or or_2 (or_2_out, controller_1_load__m__q__cnt, controller_1_dec_cnt);
  Counter #(.width(5), .max('h1f)) counter_1 (
    .load(or_2_out), .D(5'b10101), .count(controller_1_dec_cnt), .Q(counter_1_q), .clk(clk));  // open: carry, clr
  Shift_Register #(.length(21)) A (
    .shift(controller_1_shr), .in(MSB[20]), .clk(clk), .out(A_out), .load(controller_1_load_a),
    .clr(controller_1_cl__a__q_1), .d0(_21_bit_alu_p5[20]), .q0(MSB[20]), .d1(_21_bit_alu_p5[19]),
    .q1(MSB[19]), .d2(_21_bit_alu_p5[18]), .q2(MSB[18]), .d3(_21_bit_alu_p5[17]), .q3(MSB[17]),
    .d4(_21_bit_alu_p5[16]), .q4(MSB[16]), .d5(_21_bit_alu_p5[15]), .q5(MSB[15]), .d6(_21_bit_alu_p5[14]),
    .q6(MSB[14]), .d7(_21_bit_alu_p5[13]), .q7(MSB[13]), .d8(_21_bit_alu_p5[12]), .q8(MSB[12]),
    .d9(_21_bit_alu_p5[11]), .q9(MSB[11]), .d10(_21_bit_alu_p5[10]), .q10(MSB[10]), .d11(_21_bit_alu_p5[9]),
    .q11(MSB[9]), .d12(_21_bit_alu_p5[8]), .q12(MSB[8]), .d13(_21_bit_alu_p5[7]), .q13(MSB[7]),
    .d14(_21_bit_alu_p5[6]), .q14(MSB[6]), .d15(_21_bit_alu_p5[5]), .q15(MSB[5]), .d16(_21_bit_alu_p5[4]),
    .q16(MSB[4]), .d17(_21_bit_alu_p5[3]), .q17(MSB[3]), .d18(_21_bit_alu_p5[2]), .q18(MSB[2]),
    .d19(_21_bit_alu_p5[1]), .q19(MSB[1]), .d20(_21_bit_alu_p5[0]), .q20(MSB[0]));
  Shift_Register #(.length(21)) M (
    .shift(1'b0), .clk(clk), .load(controller_1_load__m__q__cnt), .d0(M_input[20]), .q0(M_q20[20]),
    .d1(M_input[19]), .q1(M_q20[19]), .d2(M_input[18]), .q2(M_q20[18]), .d3(M_input[17]), .q3(M_q20[17]),
    .d4(M_input[16]), .q4(M_q20[16]), .d5(M_input[15]), .q5(M_q20[15]), .d6(M_input[14]), .q6(M_q20[14]),
    .d7(M_input[13]), .q7(M_q20[13]), .d8(M_input[12]), .q8(M_q20[12]), .d9(M_input[11]), .q9(M_q20[11]),
    .d10(M_input[10]), .q10(M_q20[10]), .d11(M_input[9]), .q11(M_q20[9]), .d12(M_input[8]), .q12(M_q20[8]),
    .d13(M_input[7]), .q13(M_q20[7]), .d14(M_input[6]), .q14(M_q20[6]), .d15(M_input[5]), .q15(M_q20[5]),
    .d16(M_input[4]), .q16(M_q20[4]), .d17(M_input[3]), .q17(M_q20[3]), .d18(M_input[2]), .q18(M_q20[2]),
    .d19(M_input[1]), .q19(M_q20[1]), .d20(M_input[0]), .q20(M_q20[0]));  // open: in, out, clr
  // _21_bit_ALU_booths_main _21_bit_alu: pin names not known; wires that end beside it: MSB, M_q20, controller_1_c0, controller_1_c1, _21_bit_alu_p5
  Shift_Register #(.length(21)) Q (
    .shift(controller_1_shr), .in(A_out), .clk(clk), .out(Q_out), .load(controller_1_load__m__q__cnt),
    .d0(Q_input[20]), .q0(LSB[20]), .d1(Q_input[19]), .q1(LSB[19]), .d2(Q_input[18]), .q2(LSB[18]),
    .d3(Q_input[17]), .q3(LSB[17]), .d4(Q_input[16]), .q4(LSB[16]), .d5(Q_input[15]), .q5(LSB[15]),
    .d6(Q_input[14]), .q6(LSB[14]), .d7(Q_input[13]), .q7(LSB[13]), .d8(Q_input[12]), .q8(LSB[12]),
    .d9(Q_input[11]), .q9(LSB[11]), .d10(Q_input[10]), .q10(LSB[10]), .d11(Q_input[9]), .q11(LSB[9]),
    .d12(Q_input[8]), .q12(LSB[8]), .d13(Q_input[7]), .q13(LSB[7]), .d14(Q_input[6]), .q14(LSB[6]),
    .d15(Q_input[5]), .q15(LSB[5]), .d16(Q_input[4]), .q16(LSB[4]), .d17(Q_input[3]), .q17(LSB[3]),
    .d18(Q_input[2]), .q18(LSB[2]), .d19(Q_input[1]), .q19(LSB[1]), .d20(Q_input[0]), .q20(LSB[0]));  // open: clr
  Shift_Register #(.length(1)) Q__1 (
    .shift(controller_1_shr), .in(Q_out), .clk(clk), .clr(controller_1_cl__a__q_1), .q0(Q__1_q0));  // open: out, load, d0
endmodule

module Full_adder (
  input  Carry_in,
  input  A,
  input  B,
  output Result,
  output Carry_out
);

  wire and_1_out, and_2_out, xor_1_out;

  and and_1 (and_1_out, B, A);
  xor xor_1 (xor_1_out, A, B);
  or or_1 (Carry_out, and_1_out, and_2_out);
  and and_2 (and_2_out, xor_1_out, Carry_in);
  xor xor_2 (Result, Carry_in, xor_1_out);
endmodule

module _4_bit_full_adder (
  input  Carry_in,
  input  [3:0] A,
  input  [3:0] B,
  output [3:0] Result,
  output Carry
);

  wire full_adder_1_carry_out, full_adder_2_carry_out, full_adder_3_carry_out;

  Full_adder full_adder_1 (
    .Carry_in(Carry_in), .A(A[0]), .B(B[0]), .Result(Result[0]), .Carry_out(full_adder_1_carry_out));
  Full_adder full_adder_2 (
    .Carry_in(full_adder_1_carry_out), .A(A[1]), .B(B[1]), .Result(Result[1]),
    .Carry_out(full_adder_2_carry_out));
  Full_adder full_adder_3 (
    .Carry_in(full_adder_2_carry_out), .A(A[2]), .B(B[2]), .Result(Result[2]),
    .Carry_out(full_adder_3_carry_out));
  Full_adder full_adder_4 (
    .Carry_in(full_adder_3_carry_out), .A(A[3]), .B(B[3]), .Result(Result[3]), .Carry_out(Carry));
endmodule

module _4_bit_xor (
  input  Control,
  input  [3:0] B,
  output [3:0] Result
);

  wire [3:0] bit_extender_1_out;

  assign bit_extender_1_out = {{3{Control}}, Control};  // Bit_Extender bit_extender_1
  assign Result = bit_extender_1_out ^ B;  // XOR_Gate xor_1, 4 bits wide
endmodule

// 32-bit \nADD/SUB
module Add_sub (
  input  Sub,
  input  [3:0] A,
  input  [3:0] B,
  output [3:0] Result,
  output Carry,
  output Overflow
);

  wire and_1_out, and_2_out, not_1_out, not_2_out, not_3_out, sign_bit_out_1_ms_bit, sign_bit_out_2_ms_bit,
       sign_bit_out_3_ms_bit;
  wire [3:0] n4_bit_xor_1_result;

  sign_bit_out sign_bit_out_1 (.Input(A), .MS_bit(sign_bit_out_1_ms_bit));
  not not_1 (not_1_out, sign_bit_out_1_ms_bit);
  _4_bit_xor u_4_bit_xor_1 (.B(B), .Result(n4_bit_xor_1_result), .Control(Sub));
  sign_bit_out sign_bit_out_2 (.Input(n4_bit_xor_1_result), .MS_bit(sign_bit_out_2_ms_bit));
  not not_2 (not_2_out, sign_bit_out_2_ms_bit);
  _4_bit_full_adder u_4_bit_full_adder_1 (
    .A(A), .B(n4_bit_xor_1_result), .Result(Result), .Carry_in(Sub), .Carry(Carry));
  sign_bit_out sign_bit_out_3 (.Input(Result), .MS_bit(sign_bit_out_3_ms_bit));
  not not_3 (not_3_out, sign_bit_out_3_ms_bit);
  and and_1 (and_1_out, not_3_out, sign_bit_out_2_ms_bit, sign_bit_out_1_ms_bit);
  and and_2 (and_2_out, sign_bit_out_3_ms_bit, not_2_out, not_1_out);
  or or_1 (Overflow, and_1_out, and_2_out);

  // Notes on the sheet:
  //   A31
  //   B31
  //   Result 31
endmodule

// 31th
module sign_bit_out (
  input  [3:0] Input,
  output MS_bit
);


  assign MS_bit = Input[3];
endmodule

// Reduce-OR
module _4_bit_reduce_or (
  input  [3:0] Input,
  output Output
);

  or or_1 (Output, Input[0], Input[1], Input[2], Input[3]);
endmodule

// Control \nUnit
module Controller (
  input  Clk,
  input  Reset,
  input  Q0,
  input  Q_1,
  input  [4:0] Count,
  output Cl__A__Q_1,
  output LOad__M__Q__Cnt,
  output Load_A,
  output C0,
  output C1,
  output Shr,
  output Dec_Cnt
);

  wire and_3_out, multiplexer_1_out, not_1_out, not_2_out, not_3_out, not_4_out, not_5_out, not_6_out,
       not_7_out, or_2_out, Q0_prime_Q_1_out, Q0Q_1_prime_out;
  wire [1:0] rom_1_data_2;
  wire [2:0] and_1_out, and_2_out, bit_extender_1_out, bit_extender_2_out, bit_extender_3_out, CAR_q,
       or_1_out, rom_1_data;

  assign bit_extender_1_out = {{2{Q0_prime_Q_1_out}}, Q0_prime_Q_1_out};  // Bit_Extender bit_extender_1
  and Q0_prime_Q_1 (Q0_prime_Q_1_out, not_2_out, Q_1);
  not not_1 (not_1_out, Q0_prime_Q_1_out);
  assign bit_extender_2_out = {{2{not_1_out}}, not_1_out};  // Bit_Extender bit_extender_2
  assign and_1_out = 3'b100 & bit_extender_3_out & bit_extender_1_out;  // AND_Gate and_1, 3 bits wide
  assign or_1_out = and_1_out | rom_1_data | and_2_out;  // OR_Gate or_1, 3 bits wide
  not not_2 (not_2_out, Q0);
  assign and_2_out = bit_extender_2_out & bit_extender_3_out & 3'b101;  // AND_Gate and_2, 3 bits wide
  assign bit_extender_3_out = {{2{and_3_out}}, and_3_out};  // Bit_Extender bit_extender_3
  and and_3 (and_3_out, not_3_out, CAR_q[1], not_4_out);
  not not_3 (not_3_out, CAR_q[2]);
  not not_4 (not_4_out, CAR_q[0]);
  Counter #(.width(3), .max('h7)) CAR (
    .load(not_5_out), .D(or_1_out), .count(multiplexer_1_out), .Q(CAR_q), .clk(Clk), .clr(Reset));  // open: carry
  not not_5 (not_5_out, multiplexer_1_out);
  Multiplexer #(.select(2), .enable("false")) multiplexer_1 (
    .in0(1'b0), .in1(1'b1), .in2(Q0Q_1_prime_out), .in3(not_7_out), .out(multiplexer_1_out),
    .sel(rom_1_data_2));
  ROM #(.addrWidth(3), .dataWidth(12)) rom_1 (
    .addr(CAR_q), .data({Cl__A__Q_1, LOad__M__Q__Cnt, Load_A, C0, C1, Shr, Dec_Cnt, rom_1_data, rom_1_data_2}));  // open: sel
  and Q0Q_1_prime (Q0Q_1_prime_out, not_6_out, Q0);
  not not_6 (not_6_out, Q_1);
  or or_2 (or_2_out, Count[0], Count[1], Count[2], Count[3], Count[4]);
  not not_7 (not_7_out, or_2_out);

  // Notes on the sheet:
  //   To choose only
  //   state 2 (010)
  //   Control Word Format: Clear (A, Q-1), Load (M, Q, Cnt), Load A, C0, C1, Shr, Dec Cnt, Address bits (3 bit), Selection bits (2 bit)
  //   contents of rom_1 (hex, n*v repeats v):
  //   1 c01 2 394 281 61 b 1c
endmodule
