// Logisim project CPU.circ as structural Verilog: 1 circuit, main circuit cpu
module cpu (
  input  [20:0] data_in,
  input  reset,
  input  clk,
  output [6:0] addr,
  output W,
  output [20:0] data_out,
  output R
);

  wire A_B, alu_1_zero, and_1_out, and_2_out, and_3_out, B_A, B_D, B_En, clear_A, demultiplexer_1_out0, En_A,
       JF, ld_ac, MAR_B_Ad, MAR_P, MF, multiplying, or_1_out, or_2_out, or_3_out, or_4_out, P_B_AD,
       p_plus_plus, Reset_for_mul, zero_flag;
  wire [2:0] control_unit_1_out_12;
  wire [6:0] multiplexer_2_out, PC_q;
  wire [20:0] A_val, Ac_in, ALU_out, D_out, lsb, MBR_In, msb, multiplexer_1_out, multiplexer_4_out;

  Demultiplexer #(.enable("false")) demultiplexer_1 (
    .out0(demultiplexer_1_out0), .in(clk), .sel(multiplying));  // open: out1
  Register #(.width(4)) IR (.D(data_out[20:17]), .en(p_plus_plus), .clk(clk), .clr(reset));  // open: Q
  Register #(.width(21)) D (.D(msb), .en(MF), .Q(D_out), .clk(clk), .clr(reset));
  control_unit control_unit_1 (
    .IR(data_out[20:17]), .clk(demultiplexer_1_out0), .Reset(reset), .MAR_P(MAR_P), .B_M(R),
    .p_plus_plus(p_plus_plus), .MAR_B_AD(MAR_B_Ad), .B_A(B_A), .M_B(W), .P_B_AD(P_B_AD), .A__B(A_B),
    .out_12(control_unit_1_out_12), .En_A(En_A), .JF(JF), .MF(MF), .B_D(B_D), .Reset_for_mul(Reset_for_mul));
  and and_1 (and_1_out, zero_flag, JF);
  and and_2 (and_2_out, Reset_for_mul, clk);
  and and_3 (and_3_out, clk, MF);
  or or_1 (or_1_out, P_B_AD, and_1_out);
  ALU alu_1 (
    .A(A_val), .B(data_out), .c2(control_unit_1_out_12[2]), .c1(control_unit_1_out_12[1]),
    .c0(control_unit_1_out_12[0]), .Result(ALU_out), .Zero(alu_1_zero));  // open: Negative, Overflow, Carry
  or or_2 (or_2_out, and_2_out, and_3_out);
  Counter #(.width(7), .max('h7f)) PC (
    .load(or_1_out), .D(data_out[6:0]), .count(p_plus_plus), .Q(PC_q), .clk(clk), .clr(reset));  // open: carry
  Register #(.width(1)) register_1 (.D(alu_1_zero), .en(En_A), .Q(zero_flag), .clk(clk));  // open: clr
  Booth_s_multiplier booths (
    .M_input(A_val), .Q_input(data_out), .Reset(reset), .Multiplying(multiplying), .LSB(lsb), .MSB(msb),
    .clk(or_2_out));
  or or_3 (or_3_out, MAR_P, MAR_B_Ad);
  Register #(.width(21)) Ac (.D(Ac_in), .en(ld_ac), .Q(A_val), .clk(clk), .clr(or_4_out));
  or or_4 (or_4_out, reset, clear_A);
  Multiplexer #(.width(21), .enable("false")) multiplexer_1 (
    .in0(A_val), .in1(data_in), .out(multiplexer_1_out), .sel(R));
  Multiplexer #(.width(7), .enable("false")) multiplexer_2 (
    .in0(data_out[6:0]), .in1(PC_q), .out(multiplexer_2_out), .sel(MAR_P));
  Register #(.width(7)) MAR (.D(multiplexer_2_out), .en(or_3_out), .Q(addr), .clk(clk), .clr(reset));
  Register #(.width(21)) MBR (.D(MBR_In), .en(B_En), .Q(data_out), .clk(clk), .clr(reset));
  Multiplexer #(.width(21), .enable("false")) multiplexer_3 (
    .in0(multiplexer_1_out), .in1(D_out), .out(MBR_In), .sel(B_D));
  Multiplexer #(.width(21), .enable("false")) multiplexer_4 (
    .in0(ALU_out), .in1(data_out), .out(multiplexer_4_out), .sel(A_B));
  Multiplexer #(.width(21), .enable("false")) multiplexer_5 (.in0(multiplexer_4_out), .in1(lsb), .out(Ac_in), .sel(MF));
  or or_5 (B_En, R, B_D, B_A);
  or or_6 (ld_ac, En_A, A_B, MF);

  // Other names for the same wires on the sheet: B_M = R; Addr_t[6:0] = data_out[6:0]; B_val[20:0] = data_out;
  //   opcode[3:0] = data_out[20:17]; clr = reset; M_B = W

  // Notes on the sheet:
  //   unused
endmodule
