// Logisim project comp.circ as structural Verilog: 1 circuit, main circuit comp
module comp (
);

  wire button_1_out, clock_1_out, cpu_1_r, cpu_1_w;
  wire [6:0] cpu_1_addr;
  wire [20:0] cpu_1_data_out, ram_1_data;

  Button button_1 (.out(button_1_out));
  Clock clock_1 (.out(clock_1_out));
  cpu cpu_1 (
    .reset(button_1_out), .addr(cpu_1_addr), .data_out(cpu_1_data_out), .data_in(ram_1_data),
    .clk(clock_1_out), .R(cpu_1_r), .W(cpu_1_w));
  RAM #(.addrWidth(7), .dataWidth(21), .bus("separate")) ram_1 (
    .addr(cpu_1_addr), .din(cpu_1_data_out), .data(ram_1_data), .str(cpu_1_w), .clk(clock_1_out), .ld(cpu_1_r));  // open: sel, clr

  // Notes on the sheet:
  //   instruction Format: opcode(4bit)+(10 unused)+ (7bit address)
  //   AND: 0000xx
  //   ADD: 0200xx
  //   STORE_A: 0400xx
  //   OR: 0600xx
  //   SUBfrom A: 0800xx
  //   JMP 0a00xx
  //   Ld_to_Acc:   0c00xx
  //   HLT: 0exxxx
  //   JZ: 1100xx
  //   INC: 12xxxx
  //   DEC: 14xxxx
  //   XOR: 1600xx
  //   LeftShift: 1800xx
  //   STORE_D: 1a00xx
  //   MUL_with_A: 1c00xx
endmodule
