// Logisim project control_unit.circ as structural Verilog: 1 circuit, main circuit control unit
module control_unit (
  input  [3:0] IR,
  input  clk,
  input  Reset,
  output MAR_P,
  output B_M,
  output p_plus_plus,
  output MAR_B_AD,
  output B_A,
  output M_B,
  output P_B_AD,
  output A__B,
  output [2:0] out_12,
  output En_A,
  output JF,
  output MF,
  output B_D,
  output Reset_for_mul
);

  wire and_1_out, decoder_1_out8, decoder_1_out9, decoder_1_out10, decoder_1_out11, decoder_1_out12,
       decoder_1_out13, decoder_1_out14, decoder_1_out15, decoder_1_out31, not_1_out, or_1_out;
  wire [5:0] counter_1_q;
  wire [7:0] rom_1_data;

  Counter #(.width(6), .max('h3f)) counter_1 (
    .load(rom_1_data[2]), .D({IR, 2'b11}), .count(rom_1_data[0]), .Q(counter_1_q), .clk(and_1_out),
    .clr(or_1_out));  // open: carry
  or or_1 (or_1_out, rom_1_data[1], Reset);
  and and_1 (and_1_out, clk, not_1_out);
  not not_1 (not_1_out, decoder_1_out31);
  ROM #(.addrWidth(6)) rom_1 (.addr(counter_1_q), .data(rom_1_data));  // open: sel
  Decoder #(.select(5), .enable("false")) decoder_1 (
    .out0(MAR_P), .out1(B_M), .out2(p_plus_plus), .out3(MAR_B_AD), .out4(B_A), .out5(M_B), .out6(P_B_AD),
    .out7(A__B), .out8(decoder_1_out8), .out9(decoder_1_out9), .out10(decoder_1_out10),
    .out11(decoder_1_out11), .out12(decoder_1_out12), .out13(decoder_1_out13), .out14(decoder_1_out14),
    .out15(decoder_1_out15), .out16(JF), .out17(MF), .out18(B_D), .out19(Reset_for_mul),
    .out31(decoder_1_out31), .sel(rom_1_data[7:3]));  // open: out20, out21, out22, out23, out24, out25, out26, out27, out28, out29, out30
  Priority_Encoder priority_encoder_1 (
    .in0(decoder_1_out8), .in1(decoder_1_out9), .in2(decoder_1_out10), .in3(decoder_1_out11),
    .in4(decoder_1_out12), .in5(decoder_1_out13), .in6(decoder_1_out14), .in7(decoder_1_out15), .out(out_12));  // open: en_in, gs, en_out
  or or_2 (En_A, decoder_1_out8, decoder_1_out9, decoder_1_out10, decoder_1_out11, decoder_1_out12, decoder_1_out13, decoder_1_out14, decoder_1_out15, MF);

  // Notes on the sheet:
  //   contents of rom_1 (hex, n*v repeats v):
  //   1 9 14 19 9 49 2 19 9 51 2 19 21 29 2 19 9 41 2 19 9 59 2 31 2 2 2 19 9 39 2 f9 2 2 2 81 2 2 2 69 2
  //   2 2 61 2 2 2 19 9 79 2 71 2 2 2 19 91 29 2 19 9 99 89 89
  //   inc,clr,ld, flags
endmodule
